// Logisim project BasicComputer.circ as structural Verilog: 1 circuit, main circuit Basic_Computer
module Basic_Computer (
);

  RAM #(.addrWidth(12), .dataWidth(16)) ram_1 ();  // open: addr, we, oe, clk, din, dout
  // Bit16_ALSU bit16_alsu_1: pin names not known
endmodule
